# Fritzing sketch sketch (saved by Fritzing 0.9.5d)
breadboards: 1

parts:
  Mod1 = ESP32 - CAM
  U1 = LIPO-1000mAh [package=lipo-1000]
  OLED2 = OLED 128x64 I2C Monochrome Display VDD-GND
  TP1 = TP4056 [chip_label=TP4056 package="DIP (Dual Inline) [THT]"]

nets:
  GND: Mod1.GND, OLED2.GND, TP1.pin6
  N1: Mod1.IO15, OLED2.SDA
  N2: Mod1.IO14, OLED2.SCK
  VCC: Mod1.VCC, OLED2.VDD
  N3: Mod1.3V3, TP1.pin3
  N4: U1.+, TP1.pin4
  N5: U1.-, TP1.pin5

custom parts:
  ESP32 - CAM: The ESP32-CAM has a very competitive small-size camera module that can operate independently as a minimum system with a footprint of only 27*40.5*4.5mm and a deep sleep current of up to 6mA.
  OLED 128x64 I2C Monochrome Display VDD-GND: OLED 128x64 I2C Monochrome Display. Note: there are two variants of this part, this one is the VDD GND SCK SDA variant. The other is GND VDD SCK SDA. Make sure you select the part that matches your module as using the incorrect part will probably destroy your module! In addition the mounting holes are marked on silkscreen but not by default drilled. If you want drilled mounting holes, copy a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
  TP4056: A DIP stand-in part for whatever IC you want. With 6 pins on a 300mil dual inline package (DIP) footprint.
